// Logisim project alu.circ as structural Verilog: 2 circuits, main circuit alu
module alu (
  input  [31:0] A,
  input  [31:0] B,
  input  [3:0] ALUSel,
  output [31:0] Result
);

  wire [0:0] slt7;
  wire [31:0] add0, and1, divu8, mul10, mulh14, mulhu11, or2, remu9, sll6, sra5, srl4, sub12, xor3;

  Adder #(.width(32)) adder_1 (.a(A), .b(B), .out(add0));  // open: cin, cout
  assign and1 = A & B;  // AND_Gate and_1, 32 bits wide
  assign or2 = A | B;  // OR_Gate or_1, 32 bits wide
  assign xor3 = A ^ B;  // XOR_Gate xor_1, 32 bits wide
  Shifter #(.width(32), .shift("lr")) shifter_1 (.in(A), .\dist (B[4:0]), .out(srl4));
  Shifter #(.width(32), .shift("ar")) shifter_2 (.in(A), .\dist (B[4:0]), .out(sra5));
  Shifter #(.width(32)) shifter_3 (.in(A), .\dist (B[4:0]), .out(sll6));
  Comparator #(.width(32)) comparator_1 (.a(A), .b(B), .lt(slt7[0]));  // open: gt, eq
  Divider #(.width(32)) divider_1 (.a(A), .b(B), .out(divu8), .rem(remu9));  // open: upper
  Subtractor #(.width(32)) subtractor_1 (.a(A), .b(B), .out(sub12));  // open: bin, bout
  my_multiplier my_multiplier_1 (
    .input1(A), .input2(B), .output_mul(mul10), .output_mulhu(mulhu11), .output_mulh(mulh14));
  Multiplexer #(.select(4), .width(32), .enable("false")) multiplexer_1 (
    .in0(add0), .in1(and1), .in2(or2), .in3(xor3), .in4(srl4), .in5(sra5), .in6(sll6),
    .in7({{31{1'b0}}, slt7[0]}), .in8(divu8), .in9(remu9), .in10(mul10), .in11(mulhu11), .in12(sub12),
    .in13(B), .in14(mulh14), .in15({32{1'b0}}), .out(Result), .sel(ALUSel));

  // Other names for the same wires on the sheet: bsel13[31:0] = B

  // Notes on the sheet:
  //   INPUTS to your circuit
  //   DON'T CHANGE THE LOCATIONS OF THE INPUTS AND OUTPUTS!
  //   OUTPUT from your circuit
endmodule

module my_multiplier (
  input  [31:0] input1,
  input  [31:0] input2,
  output [31:0] output_mul,
  output [31:0] output_mulhu,
  output [31:0] output_mulh
);

  wire [31:0] negator_1_out, negator_2_out, output01, output10, output11;

  Negator #(.width(32)) negator_1 (.in(input1), .out(negator_1_out));
  Negator #(.width(32)) negator_2 (.in(input2), .out(negator_2_out));
  Multiplier #(.width(32)) multiplier_1 (.a(negator_1_out), .b(negator_2_out), .cout(output11));  // open: out, cin
  Multiplier #(.width(32)) multiplier_2 (.a(input1), .b(input2), .out(output_mul), .cout(output_mulhu));  // open: cin
  Multiplier #(.width(32)) multiplier_3 (.a(input1), .b({32{1'b1}}), .out(output10), .cin(output_mulhu));  // open: cout
  Multiplier #(.width(32)) multiplier_4 (.a(input2), .b({32{1'b1}}), .out(output01), .cin(output_mulhu));  // open: cout
  Multiplexer #(.select(2), .width(32), .enable("false")) multiplexer_1 (
    .in0(output_mulhu), .in1(output01), .in2(output10), .in3(output11), .out(output_mulh),
    .sel({input2[31], input1[31]}));

  // Other names for the same wires on the sheet: input_1[31:0] = input1; input_1_sign = input1[31];
  //   input_2[31:0] = input2; input_2_sign = input2[31]; output00[31:0] = output_mulhu
endmodule
