// Logisim project control_logic.circ as structural Verilog: 12 circuits, main circuit control_logic
module control_logic (
  input  [31:0] in_1,
  input  in_2,
  input  in_3,
  output out_4,
  output out_5,
  output [2:0] out_6,
  output out_7,
  output out_8,
  output out_9,
  output [3:0] out_10,
  output out_11,
  output [1:0] out_12,
  output out_13,
  output out_14
);

  PCSel_processor pcsel_processor_1 (.Opcode(in_1[6:0]), .Funct3(in_1[14:12]), .BrEq(in_2), .BrLt(in_3), .PCSel(out_4));
  RegWEn_processor regwen_processor_1 (.Opcode(in_1[6:0]), .RegWEn(out_5));
  ImmSel_processr immsel_processr_1 (.Opcode(in_1[6:0]), .Fnuct3(in_1[14:12]), .ImmSel(out_6));
  BrSel_processor brsel_processor_1 (.Opcode(in_1[6:0]), .BrSel(out_13));
  BrUn_processor brun_processor_1 (.Opcode(in_1[6:0]), .Funct3(in_1[14:12]), .BrUn(out_7));
  ASel_processor asel_processor_1 (.Opcode(in_1[6:0]), .ASel(out_8));
  BSel_processor bsel_processor_1 (.Opcode(in_1[6:0]), .BSel(out_9));
  ALU_processor alu_processor_1 (.Opcode(in_1[6:0]), .Funct3(in_1[14:12]), .Funct7(in_1[31:25]), .ALUSel(out_10));
  AddrSel_processor addrsel_processor_1 (.Opcode(in_1[6:0]), .Funct3(in_1[14:12]), .AddrSel(out_14));
  MemRW_processor memrw_processor_1 (
    .Opcode(in_1[6:0]), .Funct3(in_1[14:12]), .BrEq(in_2), .BrLt(in_3), .MemRW(out_11));
  WBSel_processor wbsel_processor_1 (.Opcode(in_1[6:0]), .Funct3(in_1[14:12]), .Funct7(in_1[31:25]), .WBSel(out_12));

  // Other names for the same wires on the sheet: AddrSel = out_14; ALUSel[3:0] = out_10; ASel = out_8; BrEq = in_2;
  //   BrLt = in_3; BrSel = out_13; BrUn = out_7; BSel = out_9; ImmSel[2:0] = out_6; inst[31:0] = in_1;
  //   Opcode[6:0] = in_1[6:0]; funct3[2:0] = in_1[14:12]; funct7[6:0] = in_1[31:25]; MemRW = out_11; PCSel = out_4;
  //   RegWEn = out_5; WBSel[1:0] = out_12

  // Notes on the sheet:
  //   INPUTS to your circuit
  //   DON'T CHANGE THE LOCATIONS OF THE INPUTS AND OUTPUTS!
  //   OUTPUT from your circuit
endmodule

module PCSel_processor (
  input  [6:0] Opcode,
  input  [2:0] Funct3,
  input  BrEq,
  input  BrLt,
  output PCSel
);

  wire and_4_out, Condition, I67, not_1_out, not_2_out, not_3_out, not_4_out, not_5_out, not_6_out, SB63,
       SB63_000, SB63_001, SB63_100, SB63_101, SB63_110, SB63_111, UJ6f;

  not not_1 (not_1_out, Opcode[2]);
  not not_2 (not_2_out, Opcode[3]);
  not not_3 (not_3_out, Opcode[4]);
  not not_4 (not_4_out, Opcode[4]);
  not not_5 (not_5_out, Opcode[3]);
  not not_6 (not_6_out, Opcode[4]);
  and and_1 (SB63, not_1_out, not_2_out, not_3_out, Opcode[5], Opcode[6]);
  and and_2 (UJ6f, Opcode[2], Opcode[3], not_4_out, Opcode[5], Opcode[6]);
  and and_3 (I67, Opcode[2], not_5_out, not_6_out, Opcode[5], Opcode[6]);
  Multiplexer #(.select(2), .enable("false")) multiplexer_1 (
    .in0(1'b0), .in1(1'b1), .in2(1'b0), .out(SB63_000), .sel({BrLt, BrEq}));  // open: in3
  Multiplexer #(.select(2), .enable("false")) multiplexer_2 (
    .in0(1'b1), .in1(1'b0), .in2(1'b1), .out(SB63_001), .sel({BrLt, BrEq}));  // open: in3
  Multiplexer #(.select(2), .enable("false")) multiplexer_3 (
    .in0(1'b0), .in1(1'b0), .in2(1'b1), .out(SB63_100), .sel({BrLt, BrEq}));  // open: in3
  Multiplexer #(.select(2), .enable("false")) multiplexer_4 (
    .in0(1'b1), .in1(1'b1), .in2(1'b0), .out(SB63_101), .sel({BrLt, BrEq}));  // open: in3
  Multiplexer #(.select(2), .enable("false")) multiplexer_5 (
    .in0(1'b0), .in1(1'b0), .in2(1'b1), .out(SB63_110), .sel({BrLt, BrEq}));  // open: in3
  Multiplexer #(.select(2), .enable("false")) multiplexer_6 (
    .in0(1'b1), .in1(1'b1), .in2(1'b0), .out(SB63_111), .sel({BrLt, BrEq}));  // open: in3
  and and_4 (and_4_out, SB63, Condition);
  Multiplexer #(.select(3), .enable("false")) multiplexer_7 (
    .in0(SB63_000), .in1(SB63_001), .in4(SB63_100), .in5(SB63_101), .in6(SB63_110), .in7(SB63_111),
    .out(Condition), .sel(Funct3));  // open: in2, in3
  or or_1 (PCSel, and_4_out, UJ6f, I67);

  // Other names for the same wires on the sheet: Br[1:0] = {BrLt, BrEq}

  // Notes on the sheet:
  //   Input
  //   output
endmodule

module RegWEn_processor (
  input  [6:0] Opcode,
  output RegWEn
);

  wire and_1_out, not_1_out, not_2_out, not_3_out;

  not not_1 (not_1_out, Opcode[2]);
  not not_2 (not_2_out, Opcode[3]);
  not not_3 (not_3_out, Opcode[4]);
  not not_4 (RegWEn, and_1_out);
  and and_1 (and_1_out, not_1_out, not_2_out, not_3_out, Opcode[5]);

  // Notes on the sheet:
  //   Input
  //   output
endmodule

module ImmSel_processr (
  input  [6:0] Opcode,
  input  [2:0] Fnuct3,
  output [2:0] ImmSel
);

  wire and_4_out, and_5_out, and_7_out, and_8_out, and_10_out, I000, IR101, not_1_out, not_2_out, not_3_out,
       not_4_out, not_5_out, not_6_out, not_7_out, not_8_out, not_9_out, not_10_out, not_11_out, not_12_out,
       not_13_out, not_14_out, not_15_out, not_16_out, not_17_out, not_18_out, not_19_out, not_20_out,
       not_21_out, not_22_out, not_23_out, S001, SB010, U011, UJ100;
  wire [2:0] bitfinder_1_index;

  not not_1 (not_1_out, Opcode[2]);
  not not_2 (not_2_out, Opcode[3]);
  not not_3 (not_3_out, Opcode[4]);
  not not_4 (not_4_out, Opcode[6]);
  not not_5 (not_5_out, Opcode[2]);
  not not_6 (not_6_out, Opcode[3]);
  not not_7 (not_7_out, Opcode[4]);
  not not_8 (not_8_out, Opcode[3]);
  not not_9 (not_9_out, Opcode[6]);
  and and_1 (S001, not_1_out, not_2_out, not_3_out, Opcode[5], not_4_out);
  and and_2 (SB010, not_5_out, not_6_out, not_7_out, Opcode[5], Opcode[6]);
  and and_3 (U011, Opcode[2], not_8_out, Opcode[4], not_9_out);
  BitFinder #(.width(6)) bitfinder_1 (
    .in({IR101, UJ100, U011, SB010, S001, I000}), .index(bitfinder_1_index));  // open: found
  not not_10 (not_10_out, Opcode[4]);
  not not_11 (not_11_out, Opcode[3]);
  not not_12 (not_12_out, Opcode[4]);
  not not_13 (not_13_out, Opcode[2]);
  not not_14 (not_14_out, Opcode[3]);
  not not_15 (not_15_out, Opcode[4]);
  not not_16 (not_16_out, Opcode[5]);
  not not_17 (not_17_out, Opcode[6]);
  not not_18 (not_18_out, Opcode[2]);
  not not_19 (not_19_out, Opcode[3]);
  not not_20 (not_20_out, Opcode[5]);
  not not_21 (not_21_out, Opcode[6]);
  not not_22 (not_22_out, Fnuct3[1]);
  and and_4 (and_4_out, not_18_out, not_19_out, not_20_out, not_21_out);
  and and_5 (and_5_out, Fnuct3[0], not_22_out);
  and and_6 (UJ100, Opcode[2], Opcode[3], not_10_out, Opcode[5], Opcode[6]);
  Multiplexer #(.select(3), .width(3), .enable("false")) multiplexer_1 (
    .in0(3'b000), .in1(3'b001), .in2(3'b010), .in3(3'b011), .in4(3'b100), .in5(3'b101), .out(ImmSel),
    .sel(bitfinder_1_index));  // open: in6, in7
  and and_7 (and_7_out, Opcode[2], not_11_out, not_12_out, Opcode[5], Opcode[6]);
  and and_8 (and_8_out, not_13_out, not_14_out, not_15_out, not_16_out, not_17_out);
  and and_9 (IR101, and_4_out, and_5_out);
  not not_23 (not_23_out, IR101);
  and and_10 (and_10_out, and_4_out, not_23_out);
  or or_1 (I000, and_7_out, and_8_out, and_10_out);

  // Other names for the same wires on the sheet: Funct3[2:0] = Fnuct3

  // Notes on the sheet:
  //   Input
  //   output
endmodule

module BrSel_processor (
  input  [6:0] Opcode,
  output BrSel
);

  wire not_1_out, not_2_out, not_3_out, not_4_out;

  not not_1 (not_1_out, Opcode[2]);
  not not_2 (not_2_out, Opcode[3]);
  not not_3 (not_3_out, Opcode[4]);
  not not_4 (not_4_out, Opcode[6]);
  and and_1 (BrSel, not_1_out, not_2_out, not_3_out, Opcode[5], not_4_out);

  // Notes on the sheet:
  //   Input
  //   output
endmodule

module BrUn_processor (
  input  [6:0] Opcode,
  input  [2:0] Funct3,
  output BrUn
);

  wire not_1_out, not_2_out, not_3_out;

  not not_1 (not_1_out, Opcode[2]);
  not not_2 (not_2_out, Opcode[3]);
  not not_3 (not_3_out, Opcode[4]);
  and and_1 (BrUn, not_1_out, not_2_out, not_3_out, Opcode[5], Opcode[6], Funct3[1], Funct3[2]);

  // Notes on the sheet:
  //   Input
  //   output
endmodule

module ASel_processor (
  input  [6:0] Opcode,
  output ASel
);

  wire not_1_out, not_2_out, not_3_out, not_4_out, not_5_out, not_6_out, SB, U, UJ;

  not not_1 (not_1_out, Opcode[2]);
  not not_2 (not_2_out, Opcode[3]);
  not not_3 (not_3_out, Opcode[4]);
  not not_4 (not_4_out, Opcode[3]);
  not not_5 (not_5_out, Opcode[6]);
  not not_6 (not_6_out, Opcode[4]);
  and and_1 (SB, not_1_out, not_2_out, not_3_out, Opcode[5], Opcode[6]);
  and and_2 (U, Opcode[2], not_4_out, Opcode[4], not_5_out);
  and and_3 (UJ, Opcode[2], Opcode[3], not_6_out, Opcode[5], Opcode[6]);
  or or_1 (ASel, SB, U, UJ);

  // Notes on the sheet:
  //   Input
  //   output
endmodule

module BSel_processor (
  input  [6:0] Opcode,
  output BSel
);

  wire and_1_out, not_1_out, not_2_out, not_3_out;

  not not_1 (not_1_out, Opcode[2]);
  not not_2 (not_2_out, Opcode[3]);
  not not_3 (not_3_out, Opcode[6]);
  and and_1 (and_1_out, not_1_out, not_2_out, Opcode[4], Opcode[5], not_3_out);
  not not_4 (BSel, and_1_out);

  // Notes on the sheet:
  //   Input
  //   output
endmodule

module ALU_processor (
  input  [6:0] Opcode,
  input  [2:0] Funct3,
  input  [6:0] Funct7,
  output [3:0] ALUSel
);

  wire ADD0, AND1, and_10_out, and_11_out, and_12_out, and_13_out, and_14_out, and_15_out, and_16_out,
       and_17_out, and_18_out, and_19_out, and_20_out, and_21_out, and_22_out, and_23_out, and_24_out,
       and_25_out, and_26_out, DIVU8, I03, I13, I13_and, I67, IR0000, MUL10, MULH14, MULHU11, not_1_out,
       not_2_out, not_3_out, not_4_out, not_5_out, not_6_out, not_7_out, not_8_out, not_9_out, not_10_out,
       not_11_out, not_12_out, not_13_out, not_14_out, not_15_out, not_16_out, not_17_out, not_18_out,
       not_19_out, not_20_out, not_21_out, not_22_out, not_23_out, not_24_out, not_25_out, not_26_out,
       not_27_out, not_28_out, not_29_out, not_30_out, not_31_out, not_32_out, not_33_out, not_34_out,
       not_35_out, not_36_out, not_37_out, not_38_out, not_39_out, not_40_out, not_41_out, not_42_out,
       not_43_out, not_44_out, not_45_out, not_46_out, not_47_out, not_48_out, not_49_out, not_50_out,
       not_51_out, not_52_out, not_53_out, not_54_out, not_55_out, not_56_out, not_57_out, not_58_out, OR2,
       or_1_out, or_2_out, or_3_out, or_4_out, or_5_out, or_6_out, R33, R33_add, R33_and, REMU9, S23, SB63,
       SLL6, SLT7, SRA5, SRL4, SUB12, U17, U37, UJ6f, XOR3;
  wire [3:0] bitfinder_1_index;

  not not_1 (not_1_out, Opcode[2]);
  not not_2 (not_2_out, Opcode[3]);
  not not_3 (not_3_out, Opcode[6]);
  not not_4 (not_4_out, Opcode[2]);
  not not_5 (not_5_out, Opcode[3]);
  not not_6 (not_6_out, Opcode[4]);
  not not_7 (not_7_out, Opcode[5]);
  not not_8 (not_8_out, Opcode[6]);
  not not_9 (not_9_out, Opcode[2]);
  not not_10 (not_10_out, Opcode[3]);
  not not_11 (not_11_out, Opcode[4]);
  not not_12 (not_12_out, Opcode[6]);
  not not_13 (not_13_out, Opcode[2]);
  not not_14 (not_14_out, Opcode[3]);
  not not_15 (not_15_out, Opcode[4]);
  not not_16 (not_16_out, Opcode[3]);
  not not_17 (not_17_out, Opcode[5]);
  not not_18 (not_18_out, Opcode[6]);
  not not_19 (not_19_out, Opcode[4]);
  not not_20 (not_20_out, Opcode[3]);
  not not_21 (not_21_out, Opcode[4]);
  and and_1 (R33, not_1_out, not_2_out, Opcode[4], Opcode[5], not_3_out);
  and and_2 (I03, not_4_out, not_5_out, not_6_out, not_7_out, not_8_out);
  and and_3 (S23, not_9_out, not_10_out, not_11_out, Opcode[5], not_12_out);
  and and_4 (SB63, not_13_out, not_14_out, not_15_out, Opcode[5], Opcode[6]);
  and and_5 (U17, Opcode[2], not_16_out, Opcode[4], not_17_out, not_18_out);
  and and_6 (UJ6f, Opcode[2], Opcode[3], not_19_out, Opcode[5], Opcode[6]);
  and and_7 (I67, Opcode[2], not_20_out, not_21_out, Opcode[5], Opcode[6]);
  BitFinder #(.width(14)) bitfinder_1 (
    .in({MULH14, SUB12, MULHU11, MUL10, REMU9, DIVU8, SLT7, SLL6, SRA5, SRL4, XOR3, OR2, AND1, ADD0}),
    .index(bitfinder_1_index));  // open: found
  Multiplexer #(.select(4), .width(4), .enable("false")) multiplexer_1 (
    .in0(4'b0000), .in1(4'b0001), .in2(4'b0010), .in3(4'b0011), .in4(4'b0100), .in5(4'b0101), .in6(4'b0110),
    .in7(4'b0111), .in8(4'b1000), .in9(4'b1001), .in10(4'b1010), .in11(4'b1011), .in12(4'b1100),
    .in13(4'b1110), .out(ALUSel), .sel(bitfinder_1_index));  // open: in14, in15
  not not_22 (not_22_out, Opcode[2]);
  not not_23 (not_23_out, Opcode[3]);
  not not_24 (not_24_out, Opcode[5]);
  not not_25 (not_25_out, Opcode[6]);
  not not_26 (not_26_out, Opcode[3]);
  not not_27 (not_27_out, Opcode[6]);
  and and_8 (I13, not_22_out, not_23_out, Opcode[4], not_24_out, not_25_out);
  and and_9 (U37, Opcode[2], not_26_out, Opcode[4], Opcode[5], not_27_out);
  not not_28 (not_28_out, Funct7[0]);
  not not_29 (not_29_out, Funct7[5]);
  not not_30 (not_30_out, Funct3[0]);
  not not_31 (not_31_out, Funct3[1]);
  not not_32 (not_32_out, Funct3[2]);
  not not_33 (not_33_out, Funct3[0]);
  not not_34 (not_34_out, Funct3[1]);
  not not_35 (not_35_out, Funct3[2]);
  not not_36 (not_36_out, Funct7[0]);
  or or_1 (or_1_out, R33, I13);
  not not_37 (not_37_out, Funct3[0]);
  or or_2 (or_2_out, R33, I13);
  not not_38 (not_38_out, Funct3[0]);
  not not_39 (not_39_out, Funct3[1]);
  or or_3 (or_3_out, R33, I13);
  not not_40 (not_40_out, Funct7[5]);
  not not_41 (not_41_out, Funct7[0]);
  not not_42 (not_42_out, Funct3[1]);
  or or_4 (or_4_out, R33, I13);
  not not_43 (not_43_out, Funct3[1]);
  or or_5 (or_5_out, R33, I13);
  not not_44 (not_44_out, Funct3[1]);
  not not_45 (not_45_out, Funct3[2]);
  or or_6 (or_6_out, R33, I13);
  not not_46 (not_46_out, Funct3[0]);
  not not_47 (not_47_out, Funct3[2]);
  not not_48 (not_48_out, Funct3[1]);
  not not_49 (not_49_out, Funct3[0]);
  not not_50 (not_50_out, Funct3[1]);
  not not_51 (not_51_out, Funct3[2]);
  not not_52 (not_52_out, Funct3[2]);
  not not_53 (not_53_out, Funct3[0]);
  not not_54 (not_54_out, Funct3[1]);
  not not_55 (not_55_out, Funct3[2]);
  not not_56 (not_56_out, Funct3[1]);
  not not_57 (not_57_out, Funct3[2]);
  and and_10 (and_10_out, not_30_out, not_31_out, not_32_out);
  and and_11 (and_11_out, not_33_out, not_34_out, not_35_out);
  and and_12 (and_12_out, Funct3[0], Funct3[1], Funct3[2]);
  and and_13 (and_13_out, Funct3[0], Funct3[1], Funct3[2]);
  and and_14 (and_14_out, not_37_out, Funct3[1], Funct3[2]);
  and and_15 (and_15_out, not_38_out, not_39_out, Funct3[2]);
  and and_16 (and_16_out, not_40_out, not_41_out);
  and and_17 (and_17_out, Funct3[0], not_42_out, Funct3[2]);
  and and_18 (and_18_out, Funct3[0], not_43_out, Funct3[2]);
  not not_58 (not_58_out, Funct7[0]);
  and and_19 (and_19_out, Funct3[0], not_44_out, not_45_out);
  and and_20 (and_20_out, not_46_out, Funct3[1], not_47_out);
  and and_21 (and_21_out, Funct3[0], not_48_out, Funct3[2]);
  and and_22 (and_22_out, Funct3[0], Funct3[1], Funct3[2]);
  and and_23 (and_23_out, not_49_out, not_50_out, not_51_out);
  and and_24 (and_24_out, Funct3[0], Funct3[1], not_52_out);
  and and_25 (and_25_out, not_53_out, not_54_out, not_55_out);
  and and_26 (and_26_out, Funct3[0], not_56_out, not_57_out);
  and and_27 (R33_add, R33, not_28_out, not_29_out, and_10_out);
  and and_28 (IR0000, I13, and_11_out);
  and and_29 (R33_and, R33, not_36_out, and_12_out);
  and and_30 (I13_and, I13, and_13_out);
  and and_31 (OR2, or_1_out, and_14_out);
  and and_32 (XOR3, or_2_out, and_15_out);
  and and_33 (SRL4, or_3_out, and_16_out, and_17_out);
  and and_34 (SRA5, or_4_out, Funct7[5], and_18_out);
  and and_35 (SLL6, or_5_out, not_58_out, and_19_out);
  and and_36 (SLT7, or_6_out, and_20_out);
  and and_37 (DIVU8, R33, Funct7[0], and_21_out);
  and and_38 (REMU9, R33, Funct7[0], and_22_out);
  and and_39 (MUL10, R33, Funct7[0], and_23_out);
  and and_40 (MULHU11, R33, Funct7[0], and_24_out);
  and and_41 (SUB12, R33, Funct7[5], and_25_out);
  and and_42 (MULH14, R33, Funct7[0], and_26_out);
  or or_7 (AND1, R33_and, I13_and);
  or or_8 (ADD0, R33_add, I03, IR0000, S23, SB63, U17, U37, UJ6f, I67);

  // Other names for the same wires on the sheet: I03_add = I03; I67_add = I67; S23_add = S23; SB63_add = SB63;
  //   U17_add = U17; U37_add = U37; UJ6f_add = UJ6f

  // Notes on the sheet:
  //   Input
  //   output
endmodule

module AddrSel_processor (
  input  [6:0] Opcode,
  input  [2:0] Funct3,
  output AddrSel
);

  wire and_1_out, and_2_out, not_1_out, not_2_out, not_3_out, not_4_out;

  not not_1 (not_1_out, Opcode[2]);
  not not_2 (not_2_out, Opcode[3]);
  not not_3 (not_3_out, Opcode[4]);
  not not_4 (not_4_out, Opcode[6]);
  and and_1 (and_1_out, Funct3[0], Funct3[1], Funct3[2]);
  and and_2 (and_2_out, not_1_out, not_2_out, not_3_out, Opcode[5], not_4_out);
  and and_3 (AddrSel, and_2_out, and_1_out);

  // Notes on the sheet:
  //   Input
  //   output
endmodule

module MemRW_processor (
  input  [6:0] Opcode,
  input  [2:0] Funct3,
  input  BrEq,
  input  BrLt,
  output MemRW
);

  wire and_2_out, and_3_out, not_1_out, not_2_out, not_3_out, not_4_out, not_5_out, not_6_out, not_7_out,
       or_1_out, S;

  not not_1 (not_1_out, Opcode[2]);
  not not_2 (not_2_out, Opcode[3]);
  not not_3 (not_3_out, Opcode[4]);
  not not_4 (not_4_out, Opcode[6]);
  and and_1 (S, not_1_out, not_2_out, not_3_out, Opcode[5], not_4_out);
  not not_5 (not_5_out, BrEq);
  not not_6 (not_6_out, Funct3[0]);
  not not_7 (not_7_out, Funct3[2]);
  and and_2 (and_2_out, not_6_out, Funct3[1], not_7_out);
  and and_3 (and_3_out, Funct3[0], Funct3[1], Funct3[2], not_5_out, BrLt);
  or or_1 (or_1_out, and_2_out, and_3_out);
  and and_4 (MemRW, S, or_1_out);

  // Notes on the sheet:
  //   Input
  //   output
endmodule

module WBSel_processor (
  input  [6:0] Opcode,
  input  [2:0] Funct3,
  input  [6:0] Funct7,
  output [1:0] WBSel
);

  wire ALU_WB, I03, I13, I67, IMM_WB, not_1_out, not_2_out, not_3_out, not_4_out, not_5_out, not_6_out,
       not_7_out, not_8_out, not_9_out, not_10_out, not_11_out, not_12_out, not_13_out, not_14_out,
       not_15_out, not_16_out, not_17_out, not_18_out, not_19_out, not_20_out, not_21_out, not_22_out,
       not_23_out, not_24_out, not_25_out, not_26_out, not_27_out, PC_PLUS_4_WB, R33, S23, SB63, U17, UJ6f;
  wire [1:0] bitfinder_1_index;

  not not_1 (not_1_out, Opcode[2]);
  not not_2 (not_2_out, Opcode[3]);
  not not_3 (not_3_out, Opcode[6]);
  not not_4 (not_4_out, Opcode[2]);
  not not_5 (not_5_out, Opcode[3]);
  not not_6 (not_6_out, Opcode[4]);
  not not_7 (not_7_out, Opcode[5]);
  not not_8 (not_8_out, Opcode[6]);
  not not_9 (not_9_out, Opcode[2]);
  not not_10 (not_10_out, Opcode[3]);
  not not_11 (not_11_out, Opcode[4]);
  not not_12 (not_12_out, Opcode[6]);
  not not_13 (not_13_out, Opcode[2]);
  not not_14 (not_14_out, Opcode[3]);
  not not_15 (not_15_out, Opcode[4]);
  not not_16 (not_16_out, Opcode[3]);
  not not_17 (not_17_out, Opcode[5]);
  not not_18 (not_18_out, Opcode[6]);
  not not_19 (not_19_out, Opcode[4]);
  not not_20 (not_20_out, Opcode[3]);
  not not_21 (not_21_out, Opcode[4]);
  and and_1 (R33, not_1_out, not_2_out, Opcode[4], Opcode[5], not_3_out);
  and and_2 (I03, not_4_out, not_5_out, not_6_out, not_7_out, not_8_out);
  and and_3 (S23, not_9_out, not_10_out, not_11_out, Opcode[5], not_12_out);
  and and_4 (SB63, not_13_out, not_14_out, not_15_out, Opcode[5], Opcode[6]);
  and and_5 (U17, Opcode[2], not_16_out, Opcode[4], not_17_out, not_18_out);
  and and_6 (UJ6f, Opcode[2], Opcode[3], not_19_out, Opcode[5], Opcode[6]);
  and and_7 (I67, Opcode[2], not_20_out, not_21_out, Opcode[5], Opcode[6]);
  not not_22 (not_22_out, Opcode[2]);
  not not_23 (not_23_out, Opcode[3]);
  not not_24 (not_24_out, Opcode[5]);
  not not_25 (not_25_out, Opcode[6]);
  not not_26 (not_26_out, Opcode[3]);
  not not_27 (not_27_out, Opcode[6]);
  and and_8 (I13, not_22_out, not_23_out, Opcode[4], not_24_out, not_25_out);
  and and_9 (IMM_WB, Opcode[2], not_26_out, Opcode[4], Opcode[5], not_27_out);
  or or_1 (ALU_WB, R33, I13, U17);
  or or_2 (PC_PLUS_4_WB, UJ6f, I67);
  BitFinder #(.width(4)) bitfinder_1 (
    .in({IMM_WB, I03, ALU_WB, PC_PLUS_4_WB}), .index(bitfinder_1_index));  // open: found
  Multiplexer #(.select(2), .width(2), .enable("false")) multiplexer_1 (
    .in0(2'b00), .in1(2'b01), .in2(2'b10), .in3(2'b11), .out(WBSel), .sel(bitfinder_1_index));

  // Other names for the same wires on the sheet: MEM_WB = I03; U37 = IMM_WB

  // Notes on the sheet:
  //   Input
  //   output
endmodule
