// Logisim project cpu.circ as structural Verilog: 2 circuits, main circuit main
module main (
  input  [31:0] INSTRUCTION,
  input  in_2,
  output [31:0] PROGRAM_COUNTER,
  output [31:0] ra,
  output [31:0] sp,
  output [31:0] t0,
  output [31:0] t1,
  output [31:0] t2,
  output [31:0] s0,
  output [31:0] s1,
  output [31:0] a0
);

  wire AddrSel, ASel, BrEq, BrLt, BrSel, BrUn, BSel, MemRW, PCSel, RegWEn;
  wire [1:0] WBSel;
  wire [2:0] ImmSel;
  wire [3:0] ALUSel;
  wire [31:0] adder_2_out, addr, ALU_OUTPUT, DATA, imm, INPUT_A, INPUT_B, inst_ID, MEM_OUTPUT,
       multiplexer_1_out, multiplexer_2_out, multiplexer_3_out, PC_ID, PC_PLUS_4, rs1, rs2, WB_DATA;

  Multiplexer #(.width(32), .enable("false")) multiplexer_1 (
    .in0(PC_PLUS_4), .in1(ALU_OUTPUT), .out(multiplexer_1_out), .sel(PCSel));
  Adder #(.width(32)) adder_1 (.a(32'h4), .b(PROGRAM_COUNTER), .out(PC_PLUS_4));  // open: cin, cout
  Register #(.width(32)) PC (.D(multiplexer_1_out), .clk(in_2), .Q(PROGRAM_COUNTER));  // open: en, clr
  control_logic control_logic_1 (
    .in_1(inst_ID), .in_2(BrEq), .in_3(BrLt), .out_4(PCSel), .out_5(RegWEn), .out_6(ImmSel), .out_7(BrUn),
    .out_8(ASel), .out_9(BSel), .out_10(ALUSel), .out_11(MemRW), .out_12(WBSel), .out_13(BrSel),
    .out_14(AddrSel));
  Register #(.width(32)) u_PC_ID (.D(PROGRAM_COUNTER), .clk(in_2), .Q(PC_ID));  // open: en, clr
  Multiplexer #(.width(32), .enable("false")) multiplexer_2 (
    .in0(INSTRUCTION), .in1(32'h13), .out(multiplexer_2_out), .sel(PCSel));
  Register #(.width(32)) register_1 (.D(multiplexer_2_out), .clk(in_2), .Q(inst_ID));  // open: en, clr
  imm_gen imm_gen_1 (.ImmSel(ImmSel), .inst(inst_ID), .imm(imm));
  regfile_main RegFile (
    .rs2(inst_ID[24:20]), .rd(inst_ID[11:7]), .Read_Data_1(rs1), .Read_Data_2(rs2), .ra(ra), .sp(sp),
    .t0(t0), .t1(t1), .t2(t2), .s0(s0), .s1(s1), .a0(a0), .rs1(inst_ID[19:15]), .Write_Data(WB_DATA),
    .RegWEn(RegWEn), .clk(in_2));
  Multiplexer #(.width(32), .enable("false")) multiplexer_3 (
    .in0(rs2), .in1(imm), .out(multiplexer_3_out), .sel(BrSel));
  Multiplexer #(.width(32), .enable("false")) multiplexer_4 (.in0(rs1), .in1(PC_ID), .out(INPUT_A), .sel(ASel));
  Multiplexer #(.width(32), .enable("false")) multiplexer_5 (.in0(rs2), .in1(imm), .out(INPUT_B), .sel(BSel));
  branch_comp branch_comp_1 (.BrEq(BrEq), .rs1(rs1), .rs2(multiplexer_3_out), .BrLt(BrLt), .BrUn(BrUn));
  alu Arithmetic_Logic_Unit (.ALUSel(ALUSel), .Result(ALU_OUTPUT), .A(INPUT_A), .B(INPUT_B));
  Multiplexer #(.width(32), .enable("false")) multiplexer_6 (.in0(rs1), .in1(ALU_OUTPUT), .out(addr), .sel(AddrSel));
  // mem_main DMEM: pin names not known; wires that end beside it: addr, rs2, in_2, MemRW, DATA
  after_DMEM after_dmem_1 (.Addr(addr), .funct3(inst_ID[14:12]), .DATA(DATA), .MEM_OUTPUT(MEM_OUTPUT));
  Adder #(.width(32)) adder_2 (.a(PC_ID), .b(32'h4), .out(adder_2_out));  // open: cin, cout
  Multiplexer #(.select(2), .width(32), .enable("false")) multiplexer_7 (
    .in0(adder_2_out), .in1(ALU_OUTPUT), .in2(MEM_OUTPUT), .in3(imm), .out(WB_DATA), .sel(WBSel));

  // Other names for the same wires on the sheet: clk = in_2

  // Notes on the sheet:
  //   Output
  //   IMEM (do **NOT** move this)
  //   Inputs
  //   It is OK to move the PC, RegFile, ALU, MEM, Branch Comp, Imm Gen, and Control Logic to wherever is most convenient for you when constructing your CPU, and to delete this text
  //   Inputs/Outputs for testing. Do **NOT** move these.
endmodule

module after_DMEM (
  input  [31:0] Addr,
  input  [2:0] funct3,
  input  [31:0] DATA,
  output [31:0] MEM_OUTPUT
);

  wire [31:0] loadByte, loadHalf;

  Multiplexer #(.select(2), .width(32), .enable("false")) multiplexer_1 (
    .in0({{25{DATA[7]}}, DATA[6:0]}), .in1({{25{DATA[15]}}, DATA[14:8]}),
    .in2({{25{DATA[23]}}, DATA[22:16]}), .in3({{25{DATA[31]}}, DATA[30:24]}), .out(loadByte), .sel(Addr[1:0]));
  Multiplexer #(.width(32), .enable("false")) multiplexer_2 (
    .in0({{17{DATA[15]}}, DATA[14:0]}), .in1({{17{DATA[31]}}, DATA[30:16]}), .out(loadHalf), .sel(Addr[0]));
  Multiplexer #(.select(3), .width(32), .enable("false")) multiplexer_3 (
    .in0(loadByte), .in1(loadHalf), .in2(DATA), .out(MEM_OUTPUT), .sel(funct3));  // open: in3, in4, in5, in6, in7

  // Other names for the same wires on the sheet: byte0[31:0] = {{25{DATA[7]}}, DATA[6:0]};
  //   half0[31:0] = {{17{DATA[15]}}, DATA[14:0]}; loadWord[31:0] = DATA; byte1[31:0] = {{25{DATA[15]}}, DATA[14:8]};
  //   byte2[31:0] = {{25{DATA[23]}}, DATA[22:16]}; half1[31:0] = {{17{DATA[31]}}, DATA[30:16]};
  //   byte3[31:0] = {{25{DATA[31]}}, DATA[30:24]}
endmodule
